// Logisim project DR.circ as structural Verilog: 5 circuits, main circuit main
module main (
  input  [3:0] in_1,
  input  Clk,
  input  reset,
  output [3:0] out_4,
  output [3:0] out_5
);

  D_Flip_Flop d_ff_1 (.clk(Clk), .D(in_1[3]), .Q(out_4[3]), .reset(reset));  // open: Qn, preset, en
  Register #(.width(4)) register_1 (.D(in_1), .Q(out_5), .clk(Clk), .clr(reset));  // open: en
  D_Flip_Flop d_ff_2 (.clk(Clk), .D(in_1[2]), .Q(out_4[2]), .reset(reset));  // open: Qn, preset, en
  D_Flip_Flop d_ff_3 (.clk(Clk), .D(in_1[1]), .Q(out_4[1]), .reset(reset));  // open: Qn, preset, en
  D_Flip_Flop d_ff_4 (.clk(Clk), .D(in_1[0]), .Q(out_4[0]), .reset(reset));  // open: Qn, preset, en
endmodule

module BR (
  input  [31:0] DataIN,
  input  [1:0] RegS,
  input  Save,
  input  [1:0] RegW,
  input  [1:0] RegT,
  output [31:0] DadoRegS,
  output [31:0] DadoRegT
);

  wire demultiplexer_1_out0, demultiplexer_1_out1, demultiplexer_1_out2, demultiplexer_1_out3;
  wire [31:0] register_1_q, register_2_q, register_3_q, register_4_q;

  Demultiplexer #(.select(2), .enable("false")) demultiplexer_1 (
    .out0(demultiplexer_1_out0), .out1(demultiplexer_1_out1), .out2(demultiplexer_1_out2),
    .out3(demultiplexer_1_out3), .in(Save), .sel(RegW));
  Register #(.width(32)) register_1 (.D(DataIN), .Q(register_1_q), .clk(demultiplexer_1_out0));  // open: en, clr
  Register #(.width(32)) register_2 (.D(DataIN), .Q(register_2_q), .clk(demultiplexer_1_out1));  // open: en, clr
  Register #(.width(32)) register_3 (.D(DataIN), .Q(register_3_q), .clk(demultiplexer_1_out2));  // open: en, clr
  Register #(.width(32)) register_4 (.D(DataIN), .Q(register_4_q), .clk(demultiplexer_1_out3));  // open: en, clr
  Multiplexer #(.select(2), .width(32), .enable("false")) multiplexer_1 (
    .in0(register_1_q), .in1(register_2_q), .in2(register_3_q), .in3(register_4_q), .out(DadoRegS), .sel(RegS));
  Multiplexer #(.select(2), .width(32), .enable("false")) multiplexer_2 (
    .in0(register_1_q), .in1(register_2_q), .in2(register_3_q), .in3(register_4_q), .out(DadoRegT), .sel(RegT));
endmodule

module UsoBR (
  input  [31:0] in_1,
  input  save,
  input  [1:0] RW,
  input  [1:0] RS,
  input  [1:0] RT,
  output [31:0] out_6,
  output [31:0] out_7
);

  BR br_1 (.Save(save), .DadoRegS(out_6), .DadoRegT(out_7), .DataIN(in_1), .RegW(RW), .RegS(RS), .RegT(RT));
endmodule

module DR (
  input  Reset,
  input  [31:0] DataIN,
  input  [4:0] RegS,
  input  Save,
  input  [4:0] RegW,
  input  [4:0] RegT,
  output [31:0] DadoRegS,
  output [31:0] DadoRegT
);

  wire demultiplexer_1_out0, demultiplexer_1_out1, demultiplexer_1_out2, demultiplexer_1_out3,
       demultiplexer_1_out4, demultiplexer_1_out5, demultiplexer_1_out6, demultiplexer_1_out7,
       demultiplexer_1_out8, demultiplexer_1_out9, demultiplexer_1_out10, demultiplexer_1_out11,
       demultiplexer_1_out12, demultiplexer_1_out13, demultiplexer_1_out14, demultiplexer_1_out15,
       demultiplexer_1_out16, demultiplexer_1_out17, demultiplexer_1_out18, demultiplexer_1_out19,
       demultiplexer_1_out20, demultiplexer_1_out21, demultiplexer_1_out22, demultiplexer_1_out23,
       demultiplexer_1_out24, demultiplexer_1_out25, demultiplexer_1_out26, demultiplexer_1_out27,
       demultiplexer_1_out28, demultiplexer_1_out29, demultiplexer_1_out30, demultiplexer_1_out31;
  wire [31:0] register_1_q, register_2_q, register_3_q, register_4_q, register_5_q, register_6_q,
       register_7_q, register_8_q, register_9_q, register_10_q, register_11_q, register_12_q, register_13_q,
       register_14_q, register_15_q, register_16_q, register_17_q, register_18_q, register_19_q,
       register_20_q, register_21_q, register_22_q, register_23_q, register_24_q, register_25_q,
       register_26_q, register_27_q, register_28_q, register_29_q, register_30_q, register_31_q,
       register_32_q;

  Demultiplexer #(.select(5), .enable("false")) demultiplexer_1 (
    .out0(demultiplexer_1_out0), .out1(demultiplexer_1_out1), .out2(demultiplexer_1_out2),
    .out3(demultiplexer_1_out3), .out4(demultiplexer_1_out4), .out5(demultiplexer_1_out5),
    .out6(demultiplexer_1_out6), .out7(demultiplexer_1_out7), .out8(demultiplexer_1_out8),
    .out9(demultiplexer_1_out9), .out10(demultiplexer_1_out10), .out11(demultiplexer_1_out11),
    .out12(demultiplexer_1_out12), .out13(demultiplexer_1_out13), .out14(demultiplexer_1_out14),
    .out15(demultiplexer_1_out15), .out16(demultiplexer_1_out16), .out17(demultiplexer_1_out17),
    .out18(demultiplexer_1_out18), .out19(demultiplexer_1_out19), .out20(demultiplexer_1_out20),
    .out21(demultiplexer_1_out21), .out22(demultiplexer_1_out22), .out23(demultiplexer_1_out23),
    .out24(demultiplexer_1_out24), .out25(demultiplexer_1_out25), .out26(demultiplexer_1_out26),
    .out27(demultiplexer_1_out27), .out28(demultiplexer_1_out28), .out29(demultiplexer_1_out29),
    .out30(demultiplexer_1_out30), .out31(demultiplexer_1_out31), .in(Save), .sel(RegW));
  Register #(.width(32)) register_1 (
    .D(DataIN), .Q(register_1_q), .clk(demultiplexer_1_out0), .clr(Reset));  // open: en
  Register #(.width(32)) register_2 (
    .D(DataIN), .Q(register_2_q), .clk(demultiplexer_1_out1), .clr(Reset));  // open: en
  Register #(.width(32)) register_3 (
    .D(DataIN), .Q(register_3_q), .clk(demultiplexer_1_out2), .clr(Reset));  // open: en
  Register #(.width(32)) register_4 (
    .D(DataIN), .Q(register_4_q), .clk(demultiplexer_1_out3), .clr(Reset));  // open: en
  Register #(.width(32)) register_5 (
    .D(DataIN), .Q(register_5_q), .clk(demultiplexer_1_out4), .clr(Reset));  // open: en
  Register #(.width(32)) register_6 (
    .D(DataIN), .Q(register_6_q), .clk(demultiplexer_1_out5), .clr(Reset));  // open: en
  Register #(.width(32)) register_7 (
    .D(DataIN), .Q(register_7_q), .clk(demultiplexer_1_out6), .clr(Reset));  // open: en
  Register #(.width(32)) register_8 (
    .D(DataIN), .Q(register_8_q), .clk(demultiplexer_1_out7), .clr(Reset));  // open: en
  Register #(.width(32)) register_9 (
    .D(DataIN), .Q(register_9_q), .clk(demultiplexer_1_out8), .clr(Reset));  // open: en
  Register #(.width(32)) register_10 (
    .D(DataIN), .Q(register_10_q), .clk(demultiplexer_1_out9), .clr(Reset));  // open: en
  Register #(.width(32)) register_11 (
    .D(DataIN), .Q(register_11_q), .clk(demultiplexer_1_out10), .clr(Reset));  // open: en
  Register #(.width(32)) register_12 (
    .D(DataIN), .Q(register_12_q), .clk(demultiplexer_1_out11), .clr(Reset));  // open: en
  Register #(.width(32)) register_13 (
    .D(DataIN), .Q(register_13_q), .clk(demultiplexer_1_out12), .clr(Reset));  // open: en
  Register #(.width(32)) register_14 (
    .D(DataIN), .Q(register_14_q), .clk(demultiplexer_1_out13), .clr(Reset));  // open: en
  Register #(.width(32)) register_15 (
    .D(DataIN), .Q(register_15_q), .clk(demultiplexer_1_out14), .clr(Reset));  // open: en
  Register #(.width(32)) register_16 (
    .D(DataIN), .Q(register_16_q), .clk(demultiplexer_1_out15), .clr(Reset));  // open: en
  Register #(.width(32)) register_17 (
    .D(DataIN), .Q(register_17_q), .clk(demultiplexer_1_out16), .clr(Reset));  // open: en
  Register #(.width(32)) register_18 (
    .D(DataIN), .Q(register_18_q), .clk(demultiplexer_1_out17), .clr(Reset));  // open: en
  Register #(.width(32)) register_19 (
    .D(DataIN), .Q(register_19_q), .clk(demultiplexer_1_out18), .clr(Reset));  // open: en
  Register #(.width(32)) register_20 (
    .D(DataIN), .Q(register_20_q), .clk(demultiplexer_1_out19), .clr(Reset));  // open: en
  Register #(.width(32)) register_21 (
    .D(DataIN), .Q(register_21_q), .clk(demultiplexer_1_out20), .clr(Reset));  // open: en
  Register #(.width(32)) register_22 (
    .D(DataIN), .Q(register_22_q), .clk(demultiplexer_1_out21), .clr(Reset));  // open: en
  Register #(.width(32)) register_23 (
    .D(DataIN), .Q(register_23_q), .clk(demultiplexer_1_out22), .clr(Reset));  // open: en
  Register #(.width(32)) register_24 (
    .D(DataIN), .Q(register_24_q), .clk(demultiplexer_1_out23), .clr(Reset));  // open: en
  Register #(.width(32)) register_25 (
    .D(DataIN), .Q(register_25_q), .clk(demultiplexer_1_out24), .clr(Reset));  // open: en
  Register #(.width(32)) register_26 (
    .D(DataIN), .Q(register_26_q), .clk(demultiplexer_1_out25), .clr(Reset));  // open: en
  Register #(.width(32)) register_27 (
    .D(DataIN), .Q(register_27_q), .clk(demultiplexer_1_out26), .clr(Reset));  // open: en
  Register #(.width(32)) register_28 (
    .D(DataIN), .Q(register_28_q), .clk(demultiplexer_1_out27), .clr(Reset));  // open: en
  Register #(.width(32)) register_29 (
    .D(DataIN), .Q(register_29_q), .clk(demultiplexer_1_out28), .clr(Reset));  // open: en
  Register #(.width(32)) register_30 (
    .D(DataIN), .Q(register_30_q), .clk(demultiplexer_1_out29), .clr(Reset));  // open: en
  Register #(.width(32)) register_31 (
    .D(DataIN), .Q(register_31_q), .clk(demultiplexer_1_out30), .clr(Reset));  // open: en
  Register #(.width(32)) register_32 (
    .D(DataIN), .Q(register_32_q), .clk(demultiplexer_1_out31), .clr(Reset));  // open: en
  Multiplexer #(.select(5), .width(32), .enable("false")) multiplexer_1 (
    .in0(register_1_q), .in1(register_2_q), .in2(register_3_q), .in3(register_4_q), .in4(register_5_q),
    .in5(register_6_q), .in6(register_7_q), .in7(register_8_q), .in8(register_9_q), .in9(register_10_q),
    .in10(register_11_q), .in11(register_12_q), .in12(register_13_q), .in13(register_14_q),
    .in14(register_15_q), .in15(register_16_q), .in16(register_17_q), .in17(register_18_q),
    .in18(register_19_q), .in19(register_20_q), .in20(register_21_q), .in21(register_22_q),
    .in22(register_23_q), .in23(register_24_q), .in24(register_25_q), .in25(register_26_q),
    .in26(register_27_q), .in27(register_28_q), .in28(register_29_q), .in29(register_30_q),
    .in30(register_31_q), .in31(register_32_q), .out(DadoRegS), .sel(RegS));
  Multiplexer #(.select(5), .width(32), .enable("false")) multiplexer_2 (
    .in0(register_1_q), .in1(register_2_q), .in2(register_3_q), .in3(register_4_q), .in4(register_5_q),
    .in5(register_6_q), .in6(register_7_q), .in7(register_8_q), .in8(register_9_q), .in9(register_10_q),
    .in10(register_11_q), .in11(register_12_q), .in12(register_13_q), .in13(register_14_q),
    .in14(register_15_q), .in15(register_16_q), .in16(register_17_q), .in17(register_18_q),
    .in18(register_19_q), .in19(register_20_q), .in20(register_21_q), .in21(register_22_q),
    .in22(register_23_q), .in23(register_24_q), .in24(register_25_q), .in25(register_26_q),
    .in26(register_27_q), .in27(register_28_q), .in28(register_29_q), .in29(register_30_q),
    .in30(register_31_q), .in31(register_32_q), .out(DadoRegT), .sel(RegT));
endmodule

module UsoDR (
  input  [4:0] RegS,
  input  Reset,
  input  [4:0] RegT,
  input  [31:0] DataIN,
  input  [4:0] RegW,
  input  Save,
  output [31:0] DadoRegS,
  output [31:0] DadoRegT
);

  DR dr_1 (
    .Save(Save), .DadoRegS(DadoRegS), .RegS(RegS), .DadoRegT(DadoRegT), .DataIN(DataIN), .Reset(Reset),
    .RegW(RegW), .RegT(RegT));

  // Notes on the sheet:
  //   DR
endmodule
