// Logisim project ULAbirinto.circ as structural Verilog
module mux64 (
  input  Canal_0,
  input  in_2,
  input  in_3,
  input  in_4,
  input  in_5,
  input  in_6,
  input  in_7,
  input  in_8,
  input  in_9,
  input  in_10,
  input  in_11,
  input  in_12,
  input  in_13,
  input  in_14,
  input  in_15,
  input  in_16,
  input  in_17,
  input  in_18,
  input  in_19,
  input  in_20,
  input  in_21,
  input  in_22,
  input  in_23,
  input  in_24,
  input  in_25,
  input  in_26,
  input  in_27,
  input  in_28,
  input  in_29,
  input  in_30,
  input  in_31,
  input  in_32,
  input  Canal_32,
  input  in_34,
  input  in_35,
  input  in_36,
  input  in_37,
  input  in_38,
  input  in_39,
  input  in_40,
  input  in_41,
  input  in_42,
  input  in_43,
  input  in_44,
  input  in_45,
  input  in_46,
  input  in_47,
  input  in_48,
  input  in_49,
  input  in_50,
  input  in_51,
  input  in_52,
  input  in_53,
  input  in_54,
  input  in_55,
  input  in_56,
  input  in_57,
  input  in_58,
  input  in_59,
  input  in_60,
  input  in_61,
  input  in_62,
  input  in_63,
  input  in_64,
  input  [5:0] Sel,
  output Saida
);

  wire multiplexer_1_out, multiplexer_2_out;

  Multiplexer #(.select(5), .enable("false")) multiplexer_1 (
    .in0(Canal_0), .in1(in_2), .in2(in_3), .in3(in_4), .in4(in_5), .in5(in_6), .in6(in_7), .in7(in_8),
    .in8(in_9), .in9(in_10), .in10(in_11), .in11(in_12), .in12(in_13), .in13(in_14), .in14(in_15),
    .in15(in_16), .in16(in_17), .in17(in_18), .in18(in_19), .in19(in_20), .in20(in_21), .in21(in_22),
    .in22(in_23), .in23(in_24), .in24(in_25), .in25(in_26), .in26(in_27), .in27(in_28), .in28(in_29),
    .in29(in_30), .in30(in_31), .in31(in_32), .out(multiplexer_1_out), .sel(Sel[4:0]));
  Multiplexer #(.select(5), .enable("false")) multiplexer_2 (
    .in0(Canal_32), .in1(in_34), .in2(in_35), .in3(in_36), .in4(in_37), .in5(in_38), .in6(in_39),
    .in7(in_40), .in8(in_41), .in9(in_42), .in10(in_43), .in11(in_44), .in12(in_45), .in13(in_46),
    .in14(in_47), .in15(in_48), .in16(in_49), .in17(in_50), .in18(in_51), .in19(in_52), .in20(in_53),
    .in21(in_54), .in22(in_55), .in23(in_56), .in24(in_57), .in25(in_58), .in26(in_59), .in27(in_60),
    .in28(in_61), .in29(in_62), .in30(in_63), .in31(in_64), .out(multiplexer_2_out), .sel(Sel[4:0]));
  Multiplexer #(.enable("false")) multiplexer_3 (
    .in0(multiplexer_1_out), .in1(multiplexer_2_out), .out(Saida), .sel(Sel[5]));
endmodule

module CelULA (
  input  a,
  input  b,
  input  CarryIN,
  input  [5:0] OpCode,
  input  [5:0] Function,
  output CarryOUT,
  output Resultado
);

  wire A_t, and_1_out, mux64_1_saida, mux64_2_saida, nor_1_out, or_1_out, somadorsubtrator_1_result,
       xor_1_out, zero_1_zerou;

  and and_1 (and_1_out, b, a);
  or or_1 (or_1_out, b, a);
  xor xor_1 (xor_1_out, b, a);
  SomadorSubtrator somadorsubtrator_1 (
    .CarryOUT(CarryOUT), .b(b), .a(a), .SUB(A_t), .Result(somadorsubtrator_1_result), .CarryIN(CarryIN));
  nor nor_1 (nor_1_out, b, a);
  mux64 mux64_1 (
    .in_5(b), .in_6(b), .in_9(somadorsubtrator_1_result), .in_13(and_1_out), .in_14(or_1_out),
    .in_15(xor_1_out), .in_17(a), .Sel(OpCode), .Saida(mux64_1_saida));  // open: Canal_0, in_2, in_3, in_4, in_7, in_8, in_10, in_11, in_12, in_16, in_18, in_19, in_20, in_21, in_22, in_23, in_24, in_25, in_26, in_27, in_28, in_29, in_30, in_31, in_32, Canal_32, in_34, in_35, in_36, in_37, in_38, in_39, in_40, in_41, in_42, in_43, in_44, in_45, in_46, in_47, in_48, in_49, in_50, in_51, in_52, in_53, in_54, in_55, in_56, in_57, in_58, in_59, in_60, in_61, in_62, in_63, in_64
  mux64 mux64_2 (
    .Canal_0(a), .in_3(a), .in_4(a), .Canal_32(somadorsubtrator_1_result), .in_35(somadorsubtrator_1_result),
    .in_37(and_1_out), .in_38(or_1_out), .in_39(xor_1_out), .in_40(nor_1_out), .Sel(Function),
    .Saida(mux64_2_saida));  // open: in_2, in_5, in_6, in_7, in_8, in_9, in_10, in_11, in_12, in_13, in_14, in_15, in_16, in_17, in_18, in_19, in_20, in_21, in_22, in_23, in_24, in_25, in_26, in_27, in_28, in_29, in_30, in_31, in_32, in_34, in_36, in_41, in_42, in_43, in_44, in_45, in_46, in_47, in_48, in_49, in_50, in_51, in_52, in_53, in_54, in_55, in_56, in_57, in_58, in_59, in_60, in_61, in_62, in_63, in_64
  SUB_detector sub_detector_1 (.out_3(A_t), .OpCode(OpCode), .Function(Function));
  Zero zero_1 (.In(OpCode), .Zerou(zero_1_zerou));
  Multiplexer #(.enable("false")) multiplexer_1 (
    .in0(mux64_1_saida), .in1(mux64_2_saida), .out(Resultado), .sel(zero_1_zerou));
endmodule

module Zero (
  input  [5:0] In,
  output Zerou
);

  nor nor_1 (Zerou, In[0], In[1], In[2], In[4], In[5], In[3]);
endmodule

module SUB_detector (
  input  [5:0] OpCode,
  input  [5:0] Function,
  output out_3
);

  and and_1 (out_3, ~OpCode[5], ~OpCode[4], ~OpCode[3], ~OpCode[2], ~OpCode[1], ~OpCode[0], Function[5], ~Function[4], ~Function[3], ~Function[2], Function[1], ~Function[0]);  // AND_Gate
endmodule

module SomadorSubtrator (
  input  b,
  input  a,
  input  CarryIN,
  input  SUB,
  output CarryOUT,
  output Result
);

  wire multiplexer_1_out, not_1_out;

  not not_1 (not_1_out, b);
  Multiplexer #(.enable("false")) multiplexer_1 (.in0(b), .in1(not_1_out), .out(multiplexer_1_out), .sel(SUB));
  Adder #(.width(1)) adder_1 (.a(a), .b(multiplexer_1_out), .out(Result), .cin(CarryIN), .cout(CarryOUT));
endmodule

module ULA_4_bts (
  input  [4:0] A,
  input  [4:0] B,
  input  [4:0] sa,
  input  [5:0] OpCode,
  input  [5:0] \function ,
  output [4:0] out_6
);

  wire celula_1_p6, celula_2_p7, celula_3_p7, celula_4_p7, celula_5_p7, SL1, sub_detector_1_out_3;
  wire [4:0] deslocadorleft_1_out;

  // CelULA celula_1: pin names not known; wires that end beside it: OpCode, B[4], \function , deslocadorleft_1_out[4], out_6[4], celula_1_p6
  deslocadorLeft deslocadorleft_1 (.IN(A), .shift_amount(sa), .SL(SL1), .OUT(deslocadorleft_1_out));
  // CelULA celula_2: pin names not known; wires that end beside it: celula_1_p6, OpCode, B[3], \function , deslocadorleft_1_out[3], out_6[3], celula_2_p7
  // CelULA celula_3: pin names not known; wires that end beside it: celula_2_p7, OpCode, B[2], \function , deslocadorleft_1_out[2], out_6[2], celula_3_p7
  // CelULA celula_4: pin names not known; wires that end beside it: celula_3_p7, OpCode, B[1], \function , deslocadorleft_1_out[1], out_6[1], celula_4_p7
  SLL_detect sll_detect_1 (.out_3(SL1), .OpCode(OpCode), .Function(\function ));
  // CelULA celula_5: pin names not known; wires that end beside it: celula_4_p7, OpCode, B[0], \function , deslocadorleft_1_out[0], out_6[0], celula_5_p7
  Multiplexer #(.enable("false")) multiplexer_1 (.in0(1'b0), .in1(1'b1), .out(celula_5_p7), .sel(sub_detector_1_out_3));
  SUB_detector sub_detector_1 (.out_3(sub_detector_1_out_3), .OpCode(OpCode), .Function(\function ));
endmodule

module SLL_detect (
  input  [5:0] OpCode,
  input  [5:0] Function,
  output out_3
);

  nor nor_1 (out_3, OpCode[5], OpCode[4], OpCode[3], OpCode[2], OpCode[1], OpCode[0], Function[5], Function[4], Function[3], Function[2], Function[1], Function[0]);
endmodule

module deslocadorLeft (
  input  [4:0] IN,
  input  SL,
  input  [4:0] shift_amount,
  output [4:0] OUT
);

  wire [4:0] multiplexer_1_out;

  Multiplexer #(.select(5), .width(5), .enable("false")) multiplexer_1 (
    .in0(IN), .in1({IN[3:0], 1'b0}), .in2({IN[2:0], 2'b00}), .in3({IN[1:0], 3'b000}), .in4({IN[0], 4'b0000}),
    .out(multiplexer_1_out), .sel(shift_amount));  // open: in5, in6, in7, in8, in9, in10, in11, in12, in13, in14, in15, in16, in17, in18, in19, in20, in21, in22, in23, in24, in25, in26, in27, in28, in29, in30, in31
  Multiplexer #(.width(5), .enable("false")) multiplexer_2 (.in0(IN), .in1(multiplexer_1_out), .out(OUT), .sel(SL));
endmodule

module SLL32 (
  input  [31:0] \Número ,
  input  Select,
  input  [4:0] Shift_amount,
  output [31:0] Resultado
);

  wire [31:0] multiplexer_2_out;

  Multiplexer #(.width(32), .enable("false")) multiplexer_1 (
    .in0(\Número ), .in1(multiplexer_2_out), .out(Resultado), .sel(Select));
  Multiplexer #(.select(5), .width(32), .enable("false")) multiplexer_2 (
    .in0(\Número ), .in1({\Número [30:0], 1'b0}), .in2({\Número [29:0], 2'b00}),
    .in3({\Número [28:0], 3'b000}), .in4({\Número [27:0], 4'b0000}), .in5({\Número [26:0], {5{1'b0}}}),
    .in6({\Número [25:0], {6{1'b0}}}), .in7({\Número [24:0], {7{1'b0}}}), .in8({\Número [23:0], {8{1'b0}}}),
    .in9({\Número [22:0], {9{1'b0}}}), .in10({\Número [21:0], {10{1'b0}}}),
    .in11({\Número [20:0], {11{1'b0}}}), .in12({\Número [19:0], {12{1'b0}}}),
    .in13({\Número [18:0], {13{1'b0}}}), .in14({\Número [17:0], {14{1'b0}}}),
    .in15({\Número [16:0], {15{1'b0}}}), .in16({\Número [15:0], {16{1'b0}}}),
    .in17({\Número [14:0], {17{1'b0}}}), .in18({\Número [13:0], {18{1'b0}}}),
    .in19({\Número [12:0], {19{1'b0}}}), .in20({\Número [11:0], {20{1'b0}}}),
    .in21({\Número [10:0], {21{1'b0}}}), .in22({\Número [9:0], {22{1'b0}}}),
    .in23({\Número [8:0], {23{1'b0}}}), .in24({\Número [7:0], {24{1'b0}}}),
    .in25({\Número [6:0], {25{1'b0}}}), .in26({\Número [5:0], {26{1'b0}}}),
    .in27({\Número [4:0], {27{1'b0}}}), .in28({\Número [3:0], {28{1'b0}}}),
    .in29({\Número [2:0], {29{1'b0}}}), .in30({\Número [1:0], {30{1'b0}}}), .in31({\Número [0], {31{1'b0}}}),
    .out(multiplexer_2_out), .sel(Shift_amount));
endmodule

module SRL_detect (
  input  [5:0] OpCode,
  input  [5:0] Function,
  output out_3
);

  and and_1 (out_3, ~OpCode[5], ~OpCode[4], ~OpCode[3], ~OpCode[2], ~OpCode[1], ~OpCode[0], ~Function[5], ~Function[4], ~Function[3], ~Function[2], Function[1], ~Function[0]);  // AND_Gate
endmodule

module SRL32 (
  input  [31:0] \Número ,
  input  Select,
  input  [4:0] Shift_amount,
  output [31:0] Resultado
);

  wire [31:0] multiplexer_2_out;

  Multiplexer #(.width(32), .enable("false")) multiplexer_1 (
    .in0(\Número ), .in1(multiplexer_2_out), .out(Resultado), .sel(Select));
  Multiplexer #(.select(5), .width(32), .enable("false")) multiplexer_2 (
    .in0({1'b0, \Número [31:1]}), .in1({2'b00, \Número [31:2]}), .in2({3'b000, \Número [31:3]}),
    .in3({4'b0000, \Número [31:4]}), .in4({{5{1'b0}}, \Número [31:5]}), .in5({{6{1'b0}}, \Número [31:6]}),
    .in6({{7{1'b0}}, \Número [31:7]}), .in7({{8{1'b0}}, \Número [31:8]}), .in8({{9{1'b0}}, \Número [31:9]}),
    .in9({{10{1'b0}}, \Número [31:10]}), .in10({{11{1'b0}}, \Número [31:11]}),
    .in11({{12{1'b0}}, \Número [31:12]}), .in12({{13{1'b0}}, \Número [31:13]}),
    .in13({{14{1'b0}}, \Número [31:14]}), .in14({{15{1'b0}}, \Número [31:15]}),
    .in15({{16{1'b0}}, \Número [31:16]}), .in16({{17{1'b0}}, \Número [31:17]}),
    .in17({{18{1'b0}}, \Número [31:18]}), .in18({{19{1'b0}}, \Número [31:19]}),
    .in19({{20{1'b0}}, \Número [31:20]}), .in20({{21{1'b0}}, \Número [31:21]}),
    .in21({{22{1'b0}}, \Número [31:22]}), .in22({{23{1'b0}}, \Número [31:23]}),
    .in23({{24{1'b0}}, \Número [31:24]}), .in24({{25{1'b0}}, \Número [31:25]}),
    .in25({{26{1'b0}}, \Número [31:26]}), .in26({{27{1'b0}}, \Número [31:27]}),
    .in27({{28{1'b0}}, \Número [31:28]}), .in28({{29{1'b0}}, \Número [31:29]}),
    .in29({{30{1'b0}}, \Número [31:30]}), .in30({{31{1'b0}}, \Número [31]}), .in31({32{1'b0}}),
    .out(multiplexer_2_out), .sel(Shift_amount));
endmodule

module SRA_detect (
  input  [5:0] OpCode,
  input  [5:0] Function,
  output out_3
);

  and and_1 (out_3, ~OpCode[5], ~OpCode[4], ~OpCode[3], ~OpCode[2], ~OpCode[1], ~OpCode[0], ~Function[5], ~Function[4], ~Function[3], ~Function[2], Function[1], Function[0]);  // AND_Gate
endmodule

module SRA32 (
  input  [31:0] \Número ,
  input  Select,
  input  [4:0] Shift_amount,
  output [31:0] Resultado
);

  wire [31:0] multiplexer_2_out;

  Multiplexer #(.width(32), .enable("false")) multiplexer_1 (
    .in0(\Número ), .in1(multiplexer_2_out), .out(Resultado), .sel(Select));
  Multiplexer #(.select(5), .width(32), .enable("false")) multiplexer_2 (
    .in0({\Número [31], 1'b0, \Número [30:1]}), .in1({\Número [31], 2'b00, \Número [30:2]}),
    .in2({\Número [31], 3'b000, \Número [30:3]}), .in3({\Número [31], 4'b0000, \Número [30:4]}),
    .in4({\Número [31], {5{1'b0}}, \Número [30:5]}), .in5({\Número [31], {6{1'b0}}, \Número [30:6]}),
    .in6({\Número [31], {7{1'b0}}, \Número [30:7]}), .in7({\Número [31], {8{1'b0}}, \Número [30:8]}),
    .in8({\Número [31], {9{1'b0}}, \Número [30:9]}), .in9({\Número [31], {10{1'b0}}, \Número [30:10]}),
    .in10({\Número [31], {11{1'b0}}, \Número [30:11]}), .in11({\Número [31], {12{1'b0}}, \Número [30:12]}),
    .in12({\Número [31], {13{1'b0}}, \Número [30:13]}), .in13({\Número [31], {14{1'b0}}, \Número [30:14]}),
    .in14({\Número [31], {15{1'b0}}, \Número [30:15]}), .in15({\Número [31], {16{1'b0}}, \Número [30:16]}),
    .in16({\Número [31], {17{1'b0}}, \Número [30:17]}), .in17({\Número [31], {18{1'b0}}, \Número [30:18]}),
    .in18({\Número [31], {19{1'b0}}, \Número [30:19]}), .in19({\Número [31], {20{1'b0}}, \Número [30:20]}),
    .in20({\Número [31], {21{1'b0}}, \Número [30:21]}), .in21({\Número [31], {22{1'b0}}, \Número [30:22]}),
    .in22({\Número [31], {23{1'b0}}, \Número [30:23]}), .in23({\Número [31], {24{1'b0}}, \Número [30:24]}),
    .in24({\Número [31], {25{1'b0}}, \Número [30:25]}), .in25({\Número [31], {26{1'b0}}, \Número [30:26]}),
    .in26({\Número [31], {27{1'b0}}, \Número [30:27]}), .in27({\Número [31], {28{1'b0}}, \Número [30:28]}),
    .in28({\Número [31], {29{1'b0}}, \Número [30:29]}), .in29({\Número [31], {30{1'b0}}, \Número [30]}),
    .in30({\Número [31], {30{1'b0}}, \Número [31]}), .in31({\Número [31], {31{1'b0}}}),
    .out(multiplexer_2_out), .sel(Shift_amount));
endmodule

module ULAbirinto (
  input  [31:0] A,
  input  [31:0] B,
  input  [4:0] Shift_amount,
  input  [5:0] OpCode,
  input  [5:0] Function,
  output Iguais,
  output Diferentes,
  output [31:0] Resultado
);

  wire ADDIA, celula_2_carryout, celula_3_carryout, celula_4_carryout, celula_5_carryout, celula_6_carryout,
       celula_7_carryout, celula_8_carryout, celula_9_carryout, celula_10_carryout, celula_11_carryout,
       celula_12_carryout, celula_13_carryout, celula_14_carryout, celula_15_carryout, celula_16_carryout,
       celula_17_carryout, celula_18_carryout, celula_19_carryout, celula_20_carryout, celula_21_carryout,
       celula_22_carryout, celula_23_carryout, celula_24_carryout, celula_25_carryout, celula_26_carryout,
       celula_27_carryout, celula_28_carryout, celula_29_carryout, celula_30_carryout, celula_31_carryout,
       celula_32_carryout, multiplexer_1_out, SLL, SRA, SRL, sub_detector_1_out_3;
  wire [31:0] addia_1_resultado, sll32_1_resultado, sra32_1_resultado, srl32_1_resultado;

  ADDIA addia_1 (.a(A), .sel(ADDIA), .resultado(addia_1_resultado));
  SLL32 sll32_1 (
    .\Número (addia_1_resultado), .Shift_amount(Shift_amount), .Select(SLL), .Resultado(sll32_1_resultado));
  SLL_detect sll_detect_1 (.out_3(SLL), .OpCode(OpCode), .Function(Function));
  SRL_detect srl_detect_1 (.out_3(SRL), .OpCode(OpCode), .Function(Function));
  SRA_detect sra_detect_1 (.out_3(SRA), .OpCode(OpCode), .Function(Function));
  ADDIA_detect addia_detect_1 (.out_3(ADDIA), .OpCode(OpCode), .Function(Function));
  SRA32 sra32_1 (
    .Resultado(sra32_1_resultado), .Select(SRA), .Shift_amount(Shift_amount), .\Número (srl32_1_resultado));
  SRL32 srl32_1 (
    .Resultado(srl32_1_resultado), .Select(SRL), .Shift_amount(Shift_amount), .\Número (sll32_1_resultado));
  CelULA celula_1 (
    .b(B[31]), .a(sra32_1_resultado[31]), .OpCode(OpCode), .Function(Function), .CarryIN(celula_3_carryout),
    .Resultado(Resultado[31]));  // open: CarryOUT
  CelULA celula_2 (
    .CarryOUT(celula_2_carryout), .b(B[29]), .a(sra32_1_resultado[29]), .OpCode(OpCode), .Function(Function),
    .CarryIN(celula_5_carryout), .Resultado(Resultado[29]));
  CelULA celula_3 (
    .CarryOUT(celula_3_carryout), .b(B[30]), .a(sra32_1_resultado[30]), .OpCode(OpCode), .Function(Function),
    .CarryIN(celula_2_carryout), .Resultado(Resultado[30]));
  CelULA celula_4 (
    .CarryOUT(celula_4_carryout), .b(B[27]), .a(sra32_1_resultado[27]), .OpCode(OpCode), .Function(Function),
    .CarryIN(celula_7_carryout), .Resultado(Resultado[27]));
  CelULA celula_5 (
    .CarryOUT(celula_5_carryout), .b(B[28]), .a(sra32_1_resultado[28]), .OpCode(OpCode), .Function(Function),
    .CarryIN(celula_4_carryout), .Resultado(Resultado[28]));
  CelULA celula_6 (
    .CarryOUT(celula_6_carryout), .b(B[25]), .a(sra32_1_resultado[25]), .OpCode(OpCode), .Function(Function),
    .CarryIN(celula_8_carryout), .Resultado(Resultado[25]));
  CelULA celula_7 (
    .CarryOUT(celula_7_carryout), .b(B[26]), .a(sra32_1_resultado[26]), .OpCode(OpCode), .Function(Function),
    .CarryIN(celula_6_carryout), .Resultado(Resultado[26]));
  CelULA celula_8 (
    .CarryOUT(celula_8_carryout), .b(B[24]), .a(sra32_1_resultado[24]), .OpCode(OpCode), .Function(Function),
    .CarryIN(celula_9_carryout), .Resultado(Resultado[24]));
  CelULA celula_9 (
    .CarryOUT(celula_9_carryout), .b(B[23]), .a(sra32_1_resultado[23]), .OpCode(OpCode), .Function(Function),
    .CarryIN(celula_10_carryout), .Resultado(Resultado[23]));
  CelULA celula_10 (
    .CarryOUT(celula_10_carryout), .b(B[22]), .a(sra32_1_resultado[22]), .OpCode(OpCode),
    .Function(Function), .CarryIN(celula_11_carryout), .Resultado(Resultado[22]));
  CelULA celula_11 (
    .CarryOUT(celula_11_carryout), .b(B[21]), .a(sra32_1_resultado[21]), .OpCode(OpCode),
    .Function(Function), .CarryIN(celula_12_carryout), .Resultado(Resultado[21]));
  CelULA celula_12 (
    .CarryOUT(celula_12_carryout), .b(B[20]), .a(sra32_1_resultado[20]), .OpCode(OpCode),
    .Function(Function), .CarryIN(celula_13_carryout), .Resultado(Resultado[20]));
  CelULA celula_13 (
    .CarryOUT(celula_13_carryout), .b(B[19]), .a(sra32_1_resultado[19]), .OpCode(OpCode),
    .Function(Function), .CarryIN(celula_14_carryout), .Resultado(Resultado[19]));
  Comparador comparador_1 (.Iguais(Iguais), .b(A), .a(B), .Diferentes(Diferentes));
  CelULA celula_14 (
    .CarryOUT(celula_14_carryout), .b(B[18]), .a(sra32_1_resultado[18]), .OpCode(OpCode),
    .Function(Function), .CarryIN(celula_15_carryout), .Resultado(Resultado[18]));
  CelULA celula_15 (
    .CarryOUT(celula_15_carryout), .b(B[17]), .a(sra32_1_resultado[17]), .OpCode(OpCode),
    .Function(Function), .CarryIN(celula_16_carryout), .Resultado(Resultado[17]));
  CelULA celula_16 (
    .CarryOUT(celula_16_carryout), .b(B[16]), .a(sra32_1_resultado[16]), .OpCode(OpCode),
    .Function(Function), .CarryIN(celula_17_carryout), .Resultado(Resultado[16]));
  CelULA celula_17 (
    .CarryOUT(celula_17_carryout), .b(B[15]), .a(sra32_1_resultado[15]), .OpCode(OpCode),
    .Function(Function), .CarryIN(celula_19_carryout), .Resultado(Resultado[15]));
  CelULA celula_18 (
    .CarryOUT(celula_18_carryout), .b(B[13]), .a(sra32_1_resultado[13]), .OpCode(OpCode),
    .Function(Function), .CarryIN(celula_21_carryout), .Resultado(Resultado[13]));
  CelULA celula_19 (
    .CarryOUT(celula_19_carryout), .b(B[14]), .a(sra32_1_resultado[14]), .OpCode(OpCode),
    .Function(Function), .CarryIN(celula_18_carryout), .Resultado(Resultado[14]));
  CelULA celula_20 (
    .CarryOUT(celula_20_carryout), .b(B[11]), .a(sra32_1_resultado[11]), .OpCode(OpCode),
    .Function(Function), .CarryIN(celula_23_carryout), .Resultado(Resultado[11]));
  CelULA celula_21 (
    .CarryOUT(celula_21_carryout), .b(B[12]), .a(sra32_1_resultado[12]), .OpCode(OpCode),
    .Function(Function), .CarryIN(celula_20_carryout), .Resultado(Resultado[12]));
  CelULA celula_22 (
    .CarryOUT(celula_22_carryout), .b(B[9]), .a(sra32_1_resultado[9]), .OpCode(OpCode), .Function(Function),
    .CarryIN(celula_25_carryout), .Resultado(Resultado[9]));
  CelULA celula_23 (
    .CarryOUT(celula_23_carryout), .b(B[10]), .a(sra32_1_resultado[10]), .OpCode(OpCode),
    .Function(Function), .CarryIN(celula_22_carryout), .Resultado(Resultado[10]));
  CelULA celula_24 (
    .CarryOUT(celula_24_carryout), .b(B[7]), .a(sra32_1_resultado[7]), .OpCode(OpCode), .Function(Function),
    .CarryIN(celula_26_carryout), .Resultado(Resultado[7]));
  CelULA celula_25 (
    .CarryOUT(celula_25_carryout), .b(B[8]), .a(sra32_1_resultado[8]), .OpCode(OpCode), .Function(Function),
    .CarryIN(celula_24_carryout), .Resultado(Resultado[8]));
  CelULA celula_26 (
    .CarryOUT(celula_26_carryout), .b(B[6]), .a(sra32_1_resultado[6]), .OpCode(OpCode), .Function(Function),
    .CarryIN(celula_27_carryout), .Resultado(Resultado[6]));
  CelULA celula_27 (
    .CarryOUT(celula_27_carryout), .b(B[5]), .a(sra32_1_resultado[5]), .OpCode(OpCode), .Function(Function),
    .CarryIN(celula_28_carryout), .Resultado(Resultado[5]));
  CelULA celula_28 (
    .CarryOUT(celula_28_carryout), .b(B[4]), .a(sra32_1_resultado[4]), .OpCode(OpCode), .Function(Function),
    .CarryIN(celula_29_carryout), .Resultado(Resultado[4]));
  CelULA celula_29 (
    .CarryOUT(celula_29_carryout), .b(B[3]), .a(sra32_1_resultado[3]), .OpCode(OpCode), .Function(Function),
    .CarryIN(celula_30_carryout), .Resultado(Resultado[3]));
  CelULA celula_30 (
    .CarryOUT(celula_30_carryout), .b(B[2]), .a(sra32_1_resultado[2]), .OpCode(OpCode), .Function(Function),
    .CarryIN(celula_31_carryout), .Resultado(Resultado[2]));
  CelULA celula_31 (
    .CarryOUT(celula_31_carryout), .b(B[1]), .a(sra32_1_resultado[1]), .OpCode(OpCode), .Function(Function),
    .CarryIN(celula_32_carryout), .Resultado(Resultado[1]));
  Multiplexer #(.enable("false")) multiplexer_1 (
    .in0(1'b0), .in1(1'b1), .out(multiplexer_1_out), .sel(sub_detector_1_out_3));
  CelULA celula_32 (
    .CarryOUT(celula_32_carryout), .b(B[0]), .a(sra32_1_resultado[0]), .OpCode(OpCode), .Function(Function),
    .CarryIN(multiplexer_1_out), .Resultado(Resultado[0]));
  SUB_detector sub_detector_1 (.out_3(sub_detector_1_out_3), .OpCode(OpCode), .Function(Function));

  // Notes on the sheet:
  //   ULAbirinto
endmodule

module Comparador (
  input  [31:0] b,
  input  [31:0] a,
  output Iguais,
  output Diferentes
);

  wire xnor_1_out, xnor_2_out, xnor_3_out, xnor_4_out, xnor_5_out, xnor_6_out, xnor_7_out, xnor_8_out,
       xnor_9_out, xnor_10_out, xnor_11_out, xnor_12_out, xnor_13_out, xnor_14_out, xnor_15_out, xnor_16_out,
       xnor_17_out, xnor_18_out, xnor_19_out, xnor_20_out, xnor_21_out, xnor_22_out, xnor_23_out,
       xnor_24_out, xnor_25_out, xnor_26_out, xnor_27_out, xnor_28_out, xnor_29_out, xnor_30_out,
       xnor_31_out, xnor_32_out;

  xnor xnor_1 (xnor_1_out, b[31], a[31]);
  xnor xnor_2 (xnor_2_out, b[30], a[30]);
  xnor xnor_3 (xnor_3_out, b[29], a[29]);
  xnor xnor_4 (xnor_4_out, b[28], a[28]);
  xnor xnor_5 (xnor_5_out, b[27], a[27]);
  xnor xnor_6 (xnor_6_out, b[26], a[26]);
  xnor xnor_7 (xnor_7_out, b[25], a[25]);
  xnor xnor_8 (xnor_8_out, b[23], a[23]);
  xnor xnor_9 (xnor_9_out, b[24], a[24]);
  xnor xnor_10 (xnor_10_out, b[21], a[21]);
  xnor xnor_11 (xnor_11_out, b[22], a[22]);
  xnor xnor_12 (xnor_12_out, b[20], a[20]);
  xnor xnor_13 (xnor_13_out, b[19], a[19]);
  xnor xnor_14 (xnor_14_out, b[18], a[18]);
  xnor xnor_15 (xnor_15_out, b[17], a[17]);
  not not_1 (Diferentes, Iguais);
  and and_1 (Iguais, xnor_1_out, xnor_2_out, xnor_3_out, xnor_4_out, xnor_5_out, xnor_6_out, xnor_7_out, xnor_9_out, xnor_8_out, xnor_11_out, xnor_10_out, xnor_12_out, xnor_13_out, xnor_14_out, xnor_15_out, xnor_17_out, xnor_16_out, xnor_18_out, xnor_19_out, xnor_20_out, xnor_21_out, xnor_23_out, xnor_22_out, xnor_25_out, xnor_24_out, xnor_26_out, xnor_27_out, xnor_29_out, xnor_28_out, xnor_31_out, xnor_30_out, xnor_32_out);
  xnor xnor_16 (xnor_16_out, b[15], a[15]);
  xnor xnor_17 (xnor_17_out, b[16], a[16]);
  xnor xnor_18 (xnor_18_out, b[14], a[14]);
  xnor xnor_19 (xnor_19_out, b[13], a[13]);
  xnor xnor_20 (xnor_20_out, b[12], a[12]);
  xnor xnor_21 (xnor_21_out, b[11], a[11]);
  xnor xnor_22 (xnor_22_out, b[9], a[9]);
  xnor xnor_23 (xnor_23_out, b[10], a[10]);
  xnor xnor_24 (xnor_24_out, b[7], a[7]);
  xnor xnor_25 (xnor_25_out, b[8], a[8]);
  xnor xnor_26 (xnor_26_out, b[6], a[6]);
  xnor xnor_27 (xnor_27_out, b[5], a[5]);
  xnor xnor_28 (xnor_28_out, b[3], a[3]);
  xnor xnor_29 (xnor_29_out, b[4], a[4]);
  xnor xnor_30 (xnor_30_out, b[1], a[1]);
  xnor xnor_31 (xnor_31_out, b[2], a[2]);
  xnor xnor_32 (xnor_32_out, b[0], a[0]);
endmodule

module ADDIA (
  input  [31:0] a,
  input  sel,
  output [31:0] resultado
);

  wire [31:0] adder_1_out;

  Adder #(.width(32)) adder_1 (.a(a), .b(32'h1), .out(adder_1_out));  // open: cin, cout
  Multiplexer #(.width(32), .enable("false")) multiplexer_1 (.in0(a), .in1(adder_1_out), .out(resultado), .sel(sel));
endmodule

module ADDIA_detect (
  input  [5:0] OpCode,
  input  [5:0] Function,
  output out_3
);

  and and_1 (out_3, ~OpCode[5], OpCode[4], ~OpCode[3], ~OpCode[2], ~OpCode[1], ~OpCode[0], ~Function[5], ~Function[4], ~Function[3], ~Function[2], ~Function[1], ~Function[0]);  // AND_Gate
endmodule

// DR
module BR (
  input  Reset,
  input  [31:0] DataIN,
  input  Save,
  input  Escreva,
  input  [4:0] RegS,
  input  [4:0] RegW,
  input  [4:0] RegT,
  output [31:0] DadoRegS,
  output [31:0] DadoRegT
);

  wire and_1_out, demultiplexer_1_out1, demultiplexer_1_out2, demultiplexer_1_out3, demultiplexer_1_out4,
       demultiplexer_1_out5, demultiplexer_1_out6, demultiplexer_1_out7, demultiplexer_1_out8,
       demultiplexer_1_out9, demultiplexer_1_out10, demultiplexer_1_out11, demultiplexer_1_out12,
       demultiplexer_1_out13, demultiplexer_1_out14, demultiplexer_1_out15, demultiplexer_1_out16,
       demultiplexer_1_out17, demultiplexer_1_out18, demultiplexer_1_out19, demultiplexer_1_out20,
       demultiplexer_1_out21, demultiplexer_1_out22, demultiplexer_1_out23, demultiplexer_1_out24,
       demultiplexer_1_out25, demultiplexer_1_out26, demultiplexer_1_out27, demultiplexer_1_out28,
       demultiplexer_1_out29, demultiplexer_1_out30, demultiplexer_1_out31;
  wire [31:0] register_1_q, register_2_q, register_3_q, register_4_q, register_5_q, register_6_q,
       register_7_q, register_8_q, register_9_q, register_10_q, register_11_q, register_12_q, register_13_q,
       register_14_q, register_15_q, register_16_q, register_17_q, register_18_q, register_19_q,
       register_20_q, register_21_q, register_22_q, register_23_q, register_24_q, register_25_q,
       register_26_q, register_27_q, register_28_q, register_29_q, register_30_q, register_31_q;

  and and_1 (and_1_out, Save, Escreva);
  Demultiplexer #(.select(5), .enable("false")) demultiplexer_1 (
    .out1(demultiplexer_1_out1), .out2(demultiplexer_1_out2), .out3(demultiplexer_1_out3),
    .out4(demultiplexer_1_out4), .out5(demultiplexer_1_out5), .out6(demultiplexer_1_out6),
    .out7(demultiplexer_1_out7), .out8(demultiplexer_1_out8), .out9(demultiplexer_1_out9),
    .out10(demultiplexer_1_out10), .out11(demultiplexer_1_out11), .out12(demultiplexer_1_out12),
    .out13(demultiplexer_1_out13), .out14(demultiplexer_1_out14), .out15(demultiplexer_1_out15),
    .out16(demultiplexer_1_out16), .out17(demultiplexer_1_out17), .out18(demultiplexer_1_out18),
    .out19(demultiplexer_1_out19), .out20(demultiplexer_1_out20), .out21(demultiplexer_1_out21),
    .out22(demultiplexer_1_out22), .out23(demultiplexer_1_out23), .out24(demultiplexer_1_out24),
    .out25(demultiplexer_1_out25), .out26(demultiplexer_1_out26), .out27(demultiplexer_1_out27),
    .out28(demultiplexer_1_out28), .out29(demultiplexer_1_out29), .out30(demultiplexer_1_out30),
    .out31(demultiplexer_1_out31), .in(and_1_out), .sel(RegW));  // open: out0
  Register #(.width(32)) register_1 (
    .D(DataIN), .Q(register_1_q), .clk(demultiplexer_1_out1), .clr(Reset));  // open: en
  Register #(.width(32)) register_2 (
    .D(DataIN), .Q(register_2_q), .clk(demultiplexer_1_out2), .clr(Reset));  // open: en
  Register #(.width(32)) register_3 (
    .D(DataIN), .Q(register_3_q), .clk(demultiplexer_1_out3), .clr(Reset));  // open: en
  Register #(.width(32)) register_4 (
    .D(DataIN), .Q(register_4_q), .clk(demultiplexer_1_out4), .clr(Reset));  // open: en
  Register #(.width(32)) register_5 (
    .D(DataIN), .Q(register_5_q), .clk(demultiplexer_1_out5), .clr(Reset));  // open: en
  Register #(.width(32)) register_6 (
    .D(DataIN), .Q(register_6_q), .clk(demultiplexer_1_out6), .clr(Reset));  // open: en
  Register #(.width(32)) register_7 (
    .D(DataIN), .Q(register_7_q), .clk(demultiplexer_1_out7), .clr(Reset));  // open: en
  Register #(.width(32)) register_8 (
    .D(DataIN), .Q(register_8_q), .clk(demultiplexer_1_out8), .clr(Reset));  // open: en
  Register #(.width(32)) register_9 (
    .D(DataIN), .Q(register_9_q), .clk(demultiplexer_1_out9), .clr(Reset));  // open: en
  Register #(.width(32)) register_10 (
    .D(DataIN), .Q(register_10_q), .clk(demultiplexer_1_out10), .clr(Reset));  // open: en
  Register #(.width(32)) register_11 (
    .D(DataIN), .Q(register_11_q), .clk(demultiplexer_1_out11), .clr(Reset));  // open: en
  Register #(.width(32)) register_12 (
    .D(DataIN), .Q(register_12_q), .clk(demultiplexer_1_out12), .clr(Reset));  // open: en
  Register #(.width(32)) register_13 (
    .D(DataIN), .Q(register_13_q), .clk(demultiplexer_1_out13), .clr(Reset));  // open: en
  Register #(.width(32)) register_14 (
    .D(DataIN), .Q(register_14_q), .clk(demultiplexer_1_out14), .clr(Reset));  // open: en
  Register #(.width(32)) register_15 (
    .D(DataIN), .Q(register_15_q), .clk(demultiplexer_1_out15), .clr(Reset));  // open: en
  Register #(.width(32)) register_16 (
    .D(DataIN), .Q(register_16_q), .clk(demultiplexer_1_out16), .clr(Reset));  // open: en
  Register #(.width(32)) register_17 (
    .D(DataIN), .Q(register_17_q), .clk(demultiplexer_1_out17), .clr(Reset));  // open: en
  Register #(.width(32)) register_18 (
    .D(DataIN), .Q(register_18_q), .clk(demultiplexer_1_out18), .clr(Reset));  // open: en
  Register #(.width(32)) register_19 (
    .D(DataIN), .Q(register_19_q), .clk(demultiplexer_1_out19), .clr(Reset));  // open: en
  Register #(.width(32)) register_20 (
    .D(DataIN), .Q(register_20_q), .clk(demultiplexer_1_out20), .clr(Reset));  // open: en
  Register #(.width(32)) register_21 (
    .D(DataIN), .Q(register_21_q), .clk(demultiplexer_1_out21), .clr(Reset));  // open: en
  Register #(.width(32)) register_22 (
    .D(DataIN), .Q(register_22_q), .clk(demultiplexer_1_out22), .clr(Reset));  // open: en
  Register #(.width(32)) register_23 (
    .D(DataIN), .Q(register_23_q), .clk(demultiplexer_1_out23), .clr(Reset));  // open: en
  Register #(.width(32)) register_24 (
    .D(DataIN), .Q(register_24_q), .clk(demultiplexer_1_out24), .clr(Reset));  // open: en
  Register #(.width(32)) register_25 (
    .D(DataIN), .Q(register_25_q), .clk(demultiplexer_1_out25), .clr(Reset));  // open: en
  Register #(.width(32)) register_26 (
    .D(DataIN), .Q(register_26_q), .clk(demultiplexer_1_out26), .clr(Reset));  // open: en
  Register #(.width(32)) register_27 (
    .D(DataIN), .Q(register_27_q), .clk(demultiplexer_1_out27), .clr(Reset));  // open: en
  Register #(.width(32)) register_28 (
    .D(DataIN), .Q(register_28_q), .clk(demultiplexer_1_out28), .clr(Reset));  // open: en
  Register #(.width(32)) register_29 (
    .D(DataIN), .Q(register_29_q), .clk(demultiplexer_1_out29), .clr(Reset));  // open: en
  Register #(.width(32)) register_30 (
    .D(DataIN), .Q(register_30_q), .clk(demultiplexer_1_out30), .clr(Reset));  // open: en
  Register #(.width(32)) register_31 (
    .D(DataIN), .Q(register_31_q), .clk(demultiplexer_1_out31), .clr(Reset));  // open: en
  Multiplexer #(.select(5), .width(32), .enable("false")) multiplexer_1 (
    .in0({32{1'b0}}), .in1(register_1_q), .in2(register_2_q), .in3(register_3_q), .in4(register_4_q),
    .in5(register_5_q), .in6(register_6_q), .in7(register_7_q), .in8(register_8_q), .in9(register_9_q),
    .in10(register_10_q), .in11(register_11_q), .in12(register_12_q), .in13(register_13_q),
    .in14(register_14_q), .in15(register_15_q), .in16(register_16_q), .in17(register_17_q),
    .in18(register_18_q), .in19(register_19_q), .in20(register_20_q), .in21(register_21_q),
    .in22(register_22_q), .in23(register_23_q), .in24(register_24_q), .in25(register_25_q),
    .in26(register_26_q), .in27(register_27_q), .in28(register_28_q), .in29(register_29_q),
    .in30(register_30_q), .in31(register_31_q), .out(DadoRegS), .sel(RegS));
  Multiplexer #(.select(5), .width(32), .enable("false")) multiplexer_2 (
    .in0({32{1'b0}}), .in1(register_1_q), .in2(register_2_q), .in3(register_3_q), .in4(register_4_q),
    .in5(register_5_q), .in6(register_6_q), .in7(register_7_q), .in8(register_8_q), .in9(register_9_q),
    .in10(register_10_q), .in11(register_11_q), .in12(register_12_q), .in13(register_13_q),
    .in14(register_14_q), .in15(register_15_q), .in16(register_16_q), .in17(register_17_q),
    .in18(register_18_q), .in19(register_19_q), .in20(register_20_q), .in21(register_21_q),
    .in22(register_22_q), .in23(register_23_q), .in24(register_24_q), .in25(register_25_q),
    .in26(register_26_q), .in27(register_27_q), .in28(register_28_q), .in29(register_29_q),
    .in30(register_30_q), .in31(register_31_q), .out(DadoRegT), .sel(RegT));

  // Notes on the sheet:
  //   + 3 no reg7
  //   + 10 no reg 8
  //   reg 7 + 3 no reg8
  //   reg8 no reg9
  //   reg 8 - 1 no reg8
  //   - 4 no reg 0
  //   reg8 + reg9 no reg9
  //   reg 7 = 3
  //   reg8 = 10
  //   reg8 = 6
  //   reg9 = 6
  //   reg8 = 5
  //   reg0 = -4
  //   reg9 = 11
endmodule

// MicP
module via_de_dados (
  input  Reset,
  input  Save,
  input  [31:0] \Instrução ,
  output [31:0] Addr
);

  wire Branch, Escreva, I, Iguais, S_Z;
  wire [4:0] RS, RT, RW, Shift_Amount;
  wire [5:0] Function, OpCode;
  wire [15:0] IMM;
  wire [31:0] br_1_dadoregs, br_1_dadoregt, \extensor_1_saída32 , multiplexer_1_out, ulabirinto_1_resultado;

  \Instrução  \instrução_1  (
    .\Instrução (\Instrução ), .IMM(IMM), .OpCode(OpCode), .RS(RS), .RT(RT), .RW(RW),
    .Shift_amount(Shift_Amount), .Function(Function), .Pode_Escrever(Escreva), .Branch(Branch), .I(I),
    .S_Z(S_Z));
  dados_memorizados dados_memorizados_1 (
    .Branch(Branch), .Iguais(Iguais), .Offset(ulabirinto_1_resultado), .Save(Save), .Reset(Reset), .Addr(Addr));
  BR br_1 (
    .DadoRegS(br_1_dadoregs), .RegS(RS), .DadoRegT(br_1_dadoregt), .DataIN(ulabirinto_1_resultado),
    .Reset(Reset), .RegW(RW), .RegT(RT), .Save(Save), .Escreva(Escreva));
  Comparador comparador_1 (.Iguais(Iguais), .b(br_1_dadoregt), .a(br_1_dadoregs));  // open: Diferentes
  Multiplexer #(.width(32), .enable("false")) multiplexer_1 (
    .in0(br_1_dadoregt), .in1(\extensor_1_saída32 ), .out(multiplexer_1_out), .sel(I));
  Extensor extensor_1 (.\Saída32 (\extensor_1_saída32 ), .Sinal_ou_Zero(S_Z), .Entrada16(IMM));
  ULAbirinto ulabirinto_1 (
    .A(br_1_dadoregs), .OpCode(OpCode), .Function(Function), .B(multiplexer_1_out),
    .Shift_amount(Shift_Amount), .Resultado(ulabirinto_1_resultado));  // open: Iguais, Diferentes
endmodule

// EXT
module Extensor (
  input  [15:0] Entrada16,
  input  Sinal_ou_Zero,
  output [31:0] \Saída32 
);

  Multiplexer #(.enable("false")) multiplexer_1 (
    .in0(1'b0), .in1(Entrada16[15]), .out(\Saída32 [31]), .sel(Sinal_ou_Zero));

  assign \Saída32 [30:0] = {{15{\Saída32 [31]}}, Entrada16};
endmodule

// I
module sinal_I (
  input  [5:0] OpCode,
  output I
);

  or or_1 (I, OpCode[0], OpCode[1], OpCode[2], OpCode[3], OpCode[4], OpCode[5]);
endmodule

// S/Z
module sinal_S_Z (
  input  [5:0] OpCode,
  output S_Z
);

  wire and_1_out, and_2_out, and_3_out;

  and and_1 (and_1_out, ~OpCode[0], ~OpCode[1], ~OpCode[2], OpCode[3], ~OpCode[4], ~OpCode[5]);  // AND_Gate
  and and_2 (and_2_out, ~OpCode[0], ~OpCode[1], OpCode[2], ~OpCode[3], ~OpCode[4], ~OpCode[5]);  // AND_Gate
  and and_3 (and_3_out, OpCode[0], ~OpCode[1], OpCode[2], ~OpCode[3], ~OpCode[4], ~OpCode[5]);  // AND_Gate
  or or_1 (S_Z, and_1_out, and_2_out, and_3_out);
endmodule

// Dist
module \Instrução  (
  input  [31:0] \Instrução ,
  output [5:0] OpCode,
  output [4:0] RS,
  output [4:0] RT,
  output [4:0] RW,
  output [4:0] Shift_amount,
  output [5:0] Function,
  output S_Z,
  output I,
  output Pode_Escrever,
  output Branch,
  output [15:0] IMM
);

  sinal_S_Z sinal_s_z_1 (.OpCode(\Instrução [31:26]), .S_Z(S_Z));
  Enable enable_1 (.OpCode(\Instrução [31:26]), .Escreva(Pode_Escrever));
  Branch branch_1 (.OpCode(\Instrução [31:26]), .Branch(Branch));
  sinal_I sinal_i_1 (.OpCode(\Instrução [31:26]), .I(I));
  Multiplexer #(.width(5), .enable("false")) multiplexer_1 (
    .in0(\Instrução [15:11]), .in1(\Instrução [20:16]), .out(RW), .sel(I));

  assign Function = \Instrução [5:0];
  assign IMM = \Instrução [15:0];
  assign OpCode = \Instrução [31:26];
  assign RS = \Instrução [25:21];
  assign RT = \Instrução [20:16];
  assign Shift_amount = \Instrução [10:6];
endmodule

// RAM
module \memória  (
  input  [31:0] Addr,
  output [31:0] \Instrução 
);

  RAM #(.dataWidth(32)) ram_1 (.addr(Addr[9:2]), .data(\Instrução ));  // open: sel, clk, ld, clr
endmodule

// PC
module dados_memorizados (
  input  Branch,
  input  Iguais,
  input  [31:0] Offset,
  input  Save,
  input  Reset,
  output [31:0] Addr
);

  wire and_1_out;
  wire [31:0] adder_1_out, multiplexer_1_out;

  Multiplexer #(.width(32), .enable("false")) multiplexer_1 (
    .in0(32'h4), .in1({Offset[29:0], 2'b00}), .out(multiplexer_1_out), .sel(and_1_out));
  and and_1 (and_1_out, Branch, Iguais);
  Register #(.width(32)) register_1 (.D(adder_1_out), .Q(Addr), .clk(Save), .clr(Reset));  // open: en
  Adder #(.width(32)) adder_1 (.a(multiplexer_1_out), .b(Addr), .out(adder_1_out));  // open: cin, cout
endmodule

module PC (
  input  Save,
  input  Reset
);

  wire [31:0] \memória_1_instrução , via_de_dados_1_addr;

  \memória  \memória_1  (.Addr(via_de_dados_1_addr), .\Instrução (\memória_1_instrução ));
  via_de_dados via_de_dados_1 (
    .Reset(Reset), .Save(Save), .\Instrução (\memória_1_instrução ), .Addr(via_de_dados_1_addr));
endmodule

// Write
module Enable (
  input  [5:0] OpCode,
  output Escreva
);

  wire and_1_out, and_2_out;

  and and_1 (and_1_out, ~OpCode[0], ~OpCode[1], OpCode[2], ~OpCode[3], ~OpCode[4], ~OpCode[5]);  // AND_Gate
  and and_2 (and_2_out, OpCode[0], ~OpCode[1], OpCode[2], ~OpCode[3], ~OpCode[3], ~OpCode[5]);  // AND_Gate
  nor nor_1 (Escreva, and_1_out, and_2_out);
endmodule

// Branch
module Branch (
  input  [5:0] OpCode,
  output Branch
);

  wire and_1_out, and_2_out;

  and and_1 (and_1_out, ~OpCode[0], ~OpCode[1], OpCode[2], ~OpCode[3], ~OpCode[4], ~OpCode[5]);  // AND_Gate
  or or_1 (Branch, and_1_out, and_2_out);
  and and_2 (and_2_out, OpCode[0], ~OpCode[1], OpCode[2], ~OpCode[3], ~OpCode[3], ~OpCode[5]);  // AND_Gate
endmodule
